// Logisim project alu.circ as structural Verilog: 2 circuits, main circuit main
module main (
  input  Eingang_Carry,
  input  Eingang_Bit_A,
  input  Eingang_Bit_B,
  input  Eingang_Carry_2,
  input  Carry_aktivieren,
  input  Eingang_Bit_A_2,
  input  Eingang_Bit_B_2,
  input  Oder_Gatter_aktivieren,
  input  Eingang_Carry_3,
  input  Carry_aktivieren_2,
  input  Eingang_Bit_A_3,
  input  Eingang_Bit_B_3,
  input  Ausgang_invertieren,
  input  Oder_Gatter_aktivieren_2,
  input  A_invertieren,
  input  B_invertieren,
  output Ausgang,
  output Ausgang_Carry,
  output Ausgang_2,
  output Ausgang_Carry_1,
  output Ausgang_3,
  output Ausgang_Carry_1_2
);

  wire and_1_out, and_2_out, and_3_out, and_4_out, and_5_out, and_6_out, and_7_out, and_8_out, and_9_out,
       and_10_out, inverter_1_out_3, inverter_2_out_3, or_5_out, xor_1_out, xor_2_out, xor_3_out, xor_5_out,
       xor_6_out;

  Inverter inverter_1 (.out_3(inverter_1_out_3), .in_2(A_invertieren), .in_1(Eingang_Bit_A_3));
  Inverter inverter_2 (.out_3(inverter_2_out_3), .in_2(B_invertieren), .in_1(Eingang_Bit_B_3));
  xor xor_1 (xor_1_out, Eingang_Bit_A, Eingang_Bit_B);
  and and_1 (and_1_out, Eingang_Bit_A, Eingang_Bit_B);
  xor xor_2 (xor_2_out, Eingang_Bit_A_2, Eingang_Bit_B_2);
  and and_2 (and_2_out, Eingang_Bit_A_2, Eingang_Bit_B_2);
  xor xor_3 (xor_3_out, inverter_1_out_3, inverter_2_out_3);
  and and_3 (and_3_out, inverter_1_out_3, inverter_2_out_3);
  or or_1 (Ausgang_Carry, and_1_out, and_6_out);
  and and_4 (and_4_out, Carry_aktivieren, Eingang_Carry_2);
  or or_2 (Ausgang_Carry_1, and_2_out, and_7_out);
  and and_5 (and_5_out, Carry_aktivieren_2, Eingang_Carry_3);
  or or_3 (Ausgang_Carry_1_2, and_3_out, and_8_out);
  xor xor_4 (Ausgang, Eingang_Carry, xor_1_out);
  and and_6 (and_6_out, Eingang_Carry, xor_1_out);
  xor xor_5 (xor_5_out, and_4_out, xor_2_out);
  and and_7 (and_7_out, and_4_out, xor_2_out);
  xor xor_6 (xor_6_out, and_5_out, xor_3_out);
  and and_8 (and_8_out, and_5_out, xor_3_out);
  or or_4 (Ausgang_2, xor_5_out, and_9_out);
  and and_9 (and_9_out, Oder_Gatter_aktivieren, and_2_out);
  or or_5 (or_5_out, xor_6_out, and_10_out);
  and and_10 (and_10_out, Oder_Gatter_aktivieren_2, and_3_out);
  Inverter inverter_3 (.out_3(Ausgang_3), .in_2(Ausgang_invertieren), .in_1(or_5_out));
endmodule

module Inverter (
  input  in_1,
  input  in_2,
  output out_3
);

  wire not_1_out;

  not not_1 (not_1_out, in_1);
  Multiplexer #(.enable("false")) multiplexer_1 (.in0(in_1), .in1(not_1_out), .out(out_3), .sel(in_2));
endmodule
